# Fritzing sketch README-Setup (saved by Fritzing 0.9.3b)
breadboards: 1

parts:
  Raspberry_Pi_Zero1 = Raspberry Pi Zero
  S1 = Pushbutton [package="[THT]"]
  S2 = Pushbutton [package="[THT]"]
  U1 = mystery part, 3 pins [chip_label=?]
  R1 = Resistor [tolerance=±5% resistance=220 package=THT]
  R2 = Resistor [tolerance=±5% resistance=220 package=THT]

nets:
  N1: Raspberry_Pi_Zero1.GPIO25, S1.Pin_2, R1.Pin_1
  N2: Raspberry_Pi_Zero1.GPIO24, S2.Pin_1, S2.Pin_2, R2.Pin_1
  N3: Raspberry_Pi_Zero1.GPIO23, U1.pin1
  N4: Raspberry_Pi_Zero1.GND, U1.pin2, R1.Pin_0, R2.Pin_0
  N5: Raspberry_Pi_Zero1.5V, S1.Pin_3, S1.Pin_4, S2.Pin_3, S2.Pin_4, U1.pin3
